# Fritzing sketch Ryanteck Motor Controller (saved by Fritzing 0.9.6b)
circuit board: 8.46667cm x 5.64444cm
perfboards: 1

parts:
  IC1 = H-Bridge [package=THT]
  JP3 = male pin header, 10 pins [form="♂ (male)"]
  JP2 = male pin header, 10 pins [form="♂ (male)"]
  Motor2 = Screw terminal - 2 pins [package=THT]
  Power = Screw terminal - 2 pins [package=THT]
  Motor1 = Screw terminal - 2 pins [package=THT]
  JP1A1 = double row male pin header, 2 pins [form="♂ (male)"]
  JP1A = male pin header, 12 pins [form="♂ (male)"]
  JP1B = male pin header, 12 pins [form="♂ (male)"]

nets:
  N1: IC1.1A, JP1A.pin7
  N2: IC1.1Y, Motor1.pin1
  N3: IC1.2Y, Motor1.pin2
  N4: IC1.2A, JP1B.pin7
  N5: IC1.VCC2, Power.pin2
  N6: IC1.3_4EN, IC1.VCC1, JP3.pin1, JP2.pin1, JP1B.pin11, JP1B.pin12
  N7: IC1.3A, JP1A.pin5
  N8: IC1.3Y, Motor2.pin1
  N9: IC1.4Y, Motor2.pin2
  N10: IC1.4A, JP1B.pin5
  N11: JP3.pin2, JP1A.pin12
  N12: JP3.pin3, JP1A.pin11
  N13: JP3.pin4, JP1A.pin10
  N14: JP3.pin5, JP1A.pin9
  N15: JP3.pin6, JP1A.pin3
  N16: JP3.pin7, JP1A.pin2
  N17: JP3.pin8, JP1A.pin1
  N18: JP2.pin2, JP1A.pin4
  N19: JP2.pin3, JP1B.pin9
  N20: JP2.pin4, JP1B.pin8
  N21: JP2.pin5, JP1B.pin4
  N22: JP2.pin6, JP1B.pin2
  N23: JP2.pin7, JP1B.pin1
  N24: JP2.pin8, JP1A1.pin2

// code stored in the sketch: Ryanteck Motor Controller.bas

