# Fritzing sketch servomotorconfig (saved by Fritzing 0.9.6b)
breadboards: 1

parts:
  Mod1 = Raspberry Pi 4B
  M1 = Dagu DGServo 9g (End View) [part_number=RS001B]
  M2 = Dagu DGServo 9g (End View) [part_number=RS001B]

nets:
  5V: Mod1.5V, M1.vcc
  GND: Mod1.GND, M1.gnd, M2.gnd
  N1: Mod1.GPIO17, M1.pulse
  N2: Mod1.GPIO18, M2.pulse
