# Fritzing sketch h-bridge (saved by Fritzing 0.9.6b)
breadboards: 1

parts:
  M1 = DC Motor
  BAT1 = BC9VPC [package=bc9vpc]
  Q1 = TRANSISTOR_NPN [package=to-92-ammo]
  Q2 = TRANSISTOR_NPN [package=to-92-ammo]
  Q3 = TRANSISTOR_NPN [package=to-92-ammo]
  Q4 = TRANSISTOR_NPN [package=to-92-ammo]
  R1 = Resistor [tolerance=±5% resistance=22k package="0603 [SMD]"]
  R2 = Resistor [tolerance=±5% resistance=22k package="0603 [SMD]"]
  R3 = Resistor [tolerance=±5% resistance=22k package="0603 [SMD]"]
  R4 = Resistor [tolerance=±5% resistance=22k package="0603 [SMD]"]
  S3 = Pushbutton [package=THT]
  S4 = Pushbutton [package=THT]

nets:
  N1: M1.pin_1, Q1.E, Q3.C
  N2: M1.pin_2, Q2.C, Q4.E
  N3: BAT1.V+, Q1.C, Q4.C, R1.Pin_0, R2.Pin_0, S3.leg0, S3.leg1, S4.leg1
  N4: BAT1.V-, Q2.E, Q3.E
  N5: Q1.B, R4.Pin_1
  N6: Q2.B, R3.Pin_1
  N7: Q3.B, R2.Pin_1
  N8: Q4.B, R1.Pin_1
  N9: R3.Pin_0, R4.Pin_0, S4.leg0
