# Fritzing sketch mycircuit (saved by Fritzing 0.9.6b)
breadboards: 2

parts:
  MCU1 = Raspberry Pi Zero
  DC1 = DC_DC_XL4016 [package=board_screw]
  BAT1 = Battery Holders [package=battcon_245mm]
  S1 = H-Bridge with L298N
  M1 = DC Motor
  S2 = SWITCH-MOMENTARY-2 [package=reed_switch_pth]
  S3 = SWITCH-MOMENTARY-2 [package=reed_switch_pth]
  S4 = Round Pushbutton

nets:
  N1: MCU1.pin_2, DC1.OUT-, S1.12V
  N2: MCU1.pin_6, MCU1.pin_34, MCU1.pin_39, BAT1.+, S1.GND, S2.1, S3.1, S4.leg1
  N3: MCU1.pin_16, S2.2
  N4: MCU1.pin_18, S3.2
  N5: MCU1.pin_22, S4.leg0
  N6: MCU1.pin_24, S1.IN4
  N7: MCU1.pin_26, S1.IN3
  N8: DC1.IN+, BAT1.-
  N9: S1.M2-01, S1.M2-02, M1.pin_1, M1.pin_2

custom parts:
  H-Bridge with L298N: h-bridge
