# Fritzing sketch mycircuitv2 (saved by Fritzing 0.9.6b)
circuit board: 8.5cm x 7cm
breadboards: 2

parts:
  MCU1 = Raspberry Pi Zero
  DC1 = DC_DC_XL4016 [package=board_screw]
  BAT1 = Battery Holders [package=battcon_245mm]
  S2 = SWITCH-MOMENTARY-2 [package=reed_switch_pth]
  S3 = SWITCH-MOMENTARY-2 [package=reed_switch_pth]
  S4 = Round Pushbutton
  M1 = DC Motor
  S1 = H-Bridge with L298N

nets:
  N1: MCU1.pin_2, MCU1.pin_4, DC1.OUT-, S1.12V
  N2: MCU1.pin_6, MCU1.pin_34, MCU1.pin_39, BAT1.+, S2.1, S3.1, S4.leg1, S1.GND
  N3: MCU1.pin_16, S2.2
  N4: MCU1.pin_18, S3.2
  N5: MCU1.pin_22, S4.leg0
  N6: MCU1.pin_24, S1.IN4
  N7: MCU1.pin_26, S1.IN3
  N8: DC1.IN+, BAT1.-
  N9: M1.pin_1, S1.M2-02
  N10: M1.pin_2, S1.M2-01

custom parts:
  H-Bridge with L298N: h-bridge
