# Fritzing sketch tink (saved by Fritzing 0.9.6b)
breadboards: 1

parts:
  BAT1 = Battery Holders [package=battcom_20mm_pth]
  BAT2 = Battery Holders [package=battcom_20mm_pth]
  BAT3 = Battery Holders [package=battcom_20mm_pth]
  BAT4 = Battery Holders [package=battcom_20mm_pth]

nets:
  N1: BAT1.-, BAT2.+
  N2: BAT2.-, BAT4.+
  N3: BAT3.+, BAT4.-

notes:
  12 Volt button battery pack
